# Fritzing sketch iotsa-Hardware-bb (saved by Fritzing 0.9.3b)
circuit board: 8.46667cm x 5.64444cm
breadboards: 3

parts:
  Bare-ESP-12F1 = Bare-ESP-12F
  FTDI = male pin header, 6 pins [form="♂ (male)"]
  PRG = Pushbutton [package="[THT]"]
  U1 = V_REG_LD1117VXX [package=78xxl]
  RST = Pushbutton [package="[THT]"]
  Pwr_Sel = female pin header, 3 pins [form="♀ (female)"]
  5v = Power Jack [package=power_jack_pth]
  C1 = Tantalum Capacitor [capacitance=10µF voltage=20V package="100 mil [THT, tantalum]"]
  C2 = Tantalum Capacitor [capacitance=10µF voltage=20V package="100 mil [THT, tantalum]"]
  J1 = female pin header, 3 pins [form="♀ (female)"]
  J4 = female pin header, 18 pins [form="♀ (female)"]  # not connected
  J2 = double row female pin header, 42 pins [form="♀ (female)"]  # not connected
  J5 = double row female pin header, 42 pins [form="♀ (female)"]  # not connected
  J6 = double row female pin header, 42 pins [form="♀ (female)"]  # not connected
  J7 = double row female pin header, 42 pins [form="♀ (female)"]  # not connected
  J8 = double row female pin header, 42 pins [form="♀ (female)"]  # not connected

nets:
  N1: Bare-ESP-12F1.REST, RST.Pin_1, RST.Pin_2
  N2: Bare-ESP-12F1.CH_PD, Bare-ESP-12F1.VCC, Bare-ESP-12F1.GPIO2, Pwr_Sel.pin2
  GND: Bare-ESP-12F1.GND, Bare-ESP-12F1.GPIO15, FTDI.pin6, PRG.Pin_3, PRG.Pin_4, U1.GND, RST.Pin_3, RST.Pin_4, 5v.GND, C1.-, C2.-
  N3: Bare-ESP-12F1.GPIO0, PRG.Pin_1, PRG.Pin_2
  N4: Bare-ESP-12F1.RXD, FTDI.pin2
  N5: Bare-ESP-12F1.TXD, FTDI.pin3
  N6: FTDI.pin4, Pwr_Sel.pin1
  N7: U1.OUT, Pwr_Sel.pin3, C2.+
  N8: U1.IN, 5v.PWR, C1.+
  N9: J1.pin1, J1.pin2, J1.pin3

custom parts:
  Bare-ESP-12F: ESP-12F with minimal breakout board for breadboard use. PCB uses bare ESP-12F.
